# Fritzing sketch relais (saved by Fritzing 0.9.3b)

parts:
  KY-1 = Keyes Relay [package=THT]
  Bauteil1 = Arduino Mega 2560 (Rev3)
  M1 = DC Motor
  VCC1 = Battery block 9V

nets:
  N1: KY-1.signal, Bauteil1.5V
  N2: KY-1.power, Bauteil1.GND
  N3: KY-1.ground, Bauteil1.D38
  N4: KY-1.NC, VCC1.-
  N5: KY-1.C, M1.pin_2

notes:
  NO
  NC

custom parts:
  Keyes Relay: The Keyes 5V relay module is suitable for SCM development, home appliance control. It uses a 5V~12V TIL control signal which can control DC / AC signal.
