# Fritzing sketch rfid (saved by Fritzing 0.9.3b)

parts:
  Bauteil1 = Arduino Mega 2560 (Rev3)
  Bauteil2 = RFID-RC522-v2

nets:
  3V3: Bauteil1.3V3, Bauteil2.3.3V
  GND: Bauteil1.GND, Bauteil2.GND
  N1: Bauteil1.D7_PWM, Bauteil2.RST
  N2: Bauteil1.D50, Bauteil2.MISO
  N3: Bauteil1.D51, Bauteil2.MOSI
  N4: Bauteil1.D52, Bauteil2.SCK

custom parts:
  RFID-RC522-v2: A simple China made RFID-RC522 Reader; do check the pin labels, as this is a MFRC522 based clone.
